// Digital circuit lab04.dig as structural Verilog
module lab04 (
  input  clk,
  input  rst,
  output [31:0] PC,
  output [5:0] opcode,
  output [4:0] src1__addr,
  output [31:0] src1__out,
  output [4:0] src2__addr,
  output [31:0] src2__out,
  output [4:0] dst__addr,
  output [31:0] dst__data
);

  wire alu__src, and_1_out, branch, mem__read, mem__to__reg, mem__write, reg__dst, reg__write, zero;
  wire [1:0] alu__op;
  wire [3:0] alu__control;
  wire [15:0] cpumemory_d2;
  wire [31:0] alu__res, alu__result, data__in, data__val, multiplexer_3_out, sign__ex, u_alu_2_result;

  gen_register #(.applicationType("IVERILOG"), .CodeFile("./gen_register.v")) u_gen_register (
    .clk(clk), .rst(rst), .write_en(clk), .data_in(data__in), .data_out(PC));
  alu #(.applicationType("IVERILOG"), .CodeFile("./alu.v")) u_alu (
    .alu_control(4'b0010), .A(PC), .B(32'h4), .result(alu__result));  // open: zero
  RAMDualAccess #(.AddrBits(8), .isProgramMemory("true"), .Bits(32)) cpumemory (
    .str(mem__write), .C(clk), .ld(mem__read), .A1(alu__res[7:0]), .Din1(src2__out), .A2(PC[9:2]),
    .D1(data__val), .D2({opcode, src1__addr, src2__addr, cpumemory_d2}));
  alu #(.applicationType("IVERILOG"), .CodeFile("./alu.v")) u_alu_2 (
    .alu_control(4'b0010), .A(alu__result), .B({sign__ex[31:2], 2'b00}), .result(u_alu_2_result));  // open: zero
  and and_1 (and_1_out, branch, zero);
  BitExtender #(.inputBits(16), .outputBits(32)) bitextender_1 (.in(cpumemory_d2), .out(sign__ex));
  Multiplexer #(.Bits(32)) multiplexer_1 (.sel(and_1_out), .in_0(alu__result), .in_1(u_alu_2_result), .out(data__in));
  Multiplexer #(.Bits(5)) multiplexer_2 (
    .sel(reg__dst), .in_0(src2__addr), .in_1(cpumemory_d2[15:11]), .out(dst__addr));
  control_unit #(.applicationType("IVERILOG"), .CodeFile("./control_unit.v")) u_control_unit (
    .instr_op(opcode), .reg_dst(reg__dst), .branch(branch), .mem_read(mem__read), .mem_to_reg(mem__to__reg),
    .alu_op(alu__op), .mem_write(mem__write), .alu_src(alu__src), .reg_write(reg__write));
  cpu_registers #(.applicationType("IVERILOG"), .CodeFile("./cpu_registers.v")) u_cpu_registers (
    .clk(clk), .rst(rst), .write_en(reg__write), .src1_addr(src1__addr), .src2_addr(src2__addr),
    .dst_addr(dst__addr), .data_in(dst__data), .src1_out(src1__out), .src2_out(src2__out));
  alu_control #(.applicationType("IVERILOG"), .CodeFile("./alu_control.v")) u_alu_control (
    .alu_op(alu__op), .funct(cpumemory_d2[5:0]), .alu_control(alu__control));
  Multiplexer #(.Bits(32)) multiplexer_3 (.sel(alu__src), .in_0(src2__out), .in_1(sign__ex), .out(multiplexer_3_out));
  alu #(.applicationType("IVERILOG"), .CodeFile("./alu.v")) u_alu_3 (
    .alu_control(alu__control), .A(src1__out), .B(multiplexer_3_out), .zero(zero), .result(alu__res));
  Multiplexer #(.Bits(32)) multiplexer_4 (.sel(mem__to__reg), .in_0(alu__res), .in_1(data__val), .out(dst__data));

  // Other names for the same wires on the sheet: op__code[5:0] = opcode; pc__out[31:0] = PC;
  //   reg__data[31:0] = dst__data

  // Notes on the sheet:
  //   Inputs
  //   PC
  //   Outputs for testing
endmodule
